// Logisim project alu.circ as structural Verilog: 1 circuit, main circuit alu
module alu (
  input  [31:0] A,
  input  [31:0] B,
  input  [3:0] ALUSel,
  output [31:0] Result
);

  wire [0:0] slt1;
  wire [31:0] add0, and1, divu0, mul0, mulh0, mulhu1, multiplier_1_cout, multiplier_2_cout, multiplier_3_out,
       multiplier_4_out, negator_1_out, negator_2_out, or0, remu1, result0, result1, result2, result3,
       result4, result5, result6, result7, result8, result9, result10, result11, result12, result13, sll0,
       sra1, srl0, sub0, xor1;

  Negator #(.width(32)) negator_1 (.in(A), .out(negator_1_out));
  Negator #(.width(32)) negator_2 (.in(B), .out(negator_2_out));
  Multiplier #(.width(32)) multiplier_1 (
    .a(negator_1_out), .b(negator_2_out), .cout(multiplier_1_cout));  // open: out, cin
  Multiplier #(.width(32)) multiplier_2 (.a(A), .b(B), .cout(multiplier_2_cout));  // open: out, cin
  Multiplier #(.width(32)) multiplier_3 (
    .a(B), .b({32{1'b1}}), .out(multiplier_3_out), .cin(multiplier_2_cout));  // open: cout
  Multiplier #(.width(32)) multiplier_4 (
    .a(A), .b({32{1'b1}}), .out(multiplier_4_out), .cin(multiplier_2_cout));  // open: cout
  assign and1 = A & B;  // AND_Gate and_1, 32 bits wide
  Adder #(.width(32)) adder_1 (.a(A), .b(B), .out(add0));  // open: cin, cout
  assign or0 = A | B;  // OR_Gate or_1, 32 bits wide
  assign xor1 = A ^ B;  // XOR_Gate xor_1, 32 bits wide
  Shifter #(.width(32), .shift("lr")) shifter_1 (.in(A), .\dist (B[4:0]), .out(srl0));
  Shifter #(.width(32), .shift("ar")) shifter_2 (.in(A), .\dist (B[4:0]), .out(sra1));
  Shifter #(.width(32)) shifter_3 (.in(A), .\dist (B[4:0]), .out(sll0));
  Comparator #(.width(32)) comparator_1 (.a(A), .b(B), .lt(slt1[0]));  // open: gt, eq
  Divider #(.width(32)) divider_1 (.a(A), .b(B), .out(divu0), .rem(remu1));  // open: upper
  Multiplier #(.width(32)) multiplier_5 (.a(A), .b(B), .out(mul0), .cout(mulhu1));  // open: cin
  Subtractor #(.width(32)) subtractor_1 (.a(A), .b(B), .out(sub0));  // open: bin, bout
  Multiplexer #(.width(32), .enable("false")) multiplexer_1 (.in0(add0), .in1(and1), .out(result0), .sel(ALUSel[0]));
  Multiplexer #(.width(32), .enable("false")) multiplexer_2 (.in0(or0), .in1(xor1), .out(result1), .sel(ALUSel[0]));
  Multiplexer #(.width(32), .enable("false")) multiplexer_3 (
    .in0(sll0), .in1({{31{1'b0}}, slt1[0]}), .out(result3), .sel(ALUSel[0]));
  Multiplexer #(.width(32), .enable("false")) multiplexer_4 (.in0(srl0), .in1(sra1), .out(result2), .sel(ALUSel[0]));
  Multiplexer #(.width(32), .enable("false")) multiplexer_5 (.in0(divu0), .in1(remu1), .out(result4), .sel(ALUSel[0]));
  Multiplexer #(.width(32), .enable("false")) multiplexer_6 (.in0(mul0), .in1(mulhu1), .out(result5), .sel(ALUSel[0]));
  Multiplexer #(.width(32), .enable("false")) multiplexer_7 (.in0(sub0), .in1(B), .out(result6), .sel(ALUSel[0]));
  Multiplexer #(.width(32), .enable("false")) multiplexer_8 (.in0(mulh0), .in1(B), .out(result7), .sel(ALUSel[0]));
  Multiplexer #(.select(2), .width(32), .enable("false")) multiplexer_9 (
    .in0(multiplier_2_cout), .in1(multiplier_3_out), .in2(multiplier_4_out), .in3(multiplier_1_cout),
    .out(mulh0), .sel({B[31], A[31]}));
  Multiplexer #(.width(32), .enable("false")) multiplexer_10 (
    .in0(result0), .in1(result1), .out(result8), .sel(ALUSel[1]));
  Multiplexer #(.width(32), .enable("false")) multiplexer_11 (
    .in0(result2), .in1(result3), .out(result9), .sel(ALUSel[1]));
  Multiplexer #(.width(32), .enable("false")) multiplexer_12 (
    .in0(result4), .in1(result5), .out(result10), .sel(ALUSel[1]));
  Multiplexer #(.width(32), .enable("false")) multiplexer_13 (
    .in0(result6), .in1(result7), .out(result11), .sel(ALUSel[1]));
  Multiplexer #(.width(32), .enable("false")) multiplexer_14 (
    .in0(result8), .in1(result9), .out(result12), .sel(ALUSel[2]));
  Multiplexer #(.width(32), .enable("false")) multiplexer_15 (
    .in0(result10), .in1(result11), .out(result13), .sel(ALUSel[2]));
  Multiplexer #(.width(32), .enable("false")) multiplexer_16 (
    .in0(result12), .in1(result13), .out(Result), .sel(ALUSel[3]));

  // Other names for the same wires on the sheet: bsel1[31:0] = B; bit0 = ALUSel[0]; bit1 = ALUSel[1];
  //   bit2 = ALUSel[2]; bit3 = ALUSel[3]

  // Notes on the sheet:
  //   INPUTS to your circuit
  //   DON'T CHANGE THE LOCATIONS OF THE INPUTS AND OUTPUTS!
  //   DON'T CHANGE THE LOCATIONS OF THE INPUTS AND OUTPUTS!
  //   OUTPUT from your circuit
endmodule
