// Logisim project cpu.circ as structural Verilog: 1 circuit, main circuit main
module main (
  input  [31:0] INSTRUCTION,
  input  CLOCK,
  output [31:0] PROGRAM_COUNTER,
  output [31:0] ra,
  output [31:0] sp,
  output [31:0] t0,
  output [31:0] t1,
  output [31:0] t2,
  output [31:0] s0,
  output [31:0] s1,
  output [31:0] a0
);

  wire DMEM_p1;
  wire [4:0] rd, rs1;
  wire [31:0] aluR, imm, pc4, RegFile_read_data_1, register_1_q;

  // control_logic control_logic_1: pin names not known
  Adder #(.width(32)) adder_1 (.a(PROGRAM_COUNTER), .b(32'h4), .out(pc4));  // open: cin, cout
  Register #(.width(32)) PC (.D(pc4), .clk(CLOCK), .Q(PROGRAM_COUNTER));  // open: en, clr
  // branch_comp branch_comp_1: pin names not known
  Register #(.width(32)) register_1 (
    .D(INSTRUCTION), .clk(CLOCK), .Q({register_1_q[31:20], rs1, register_1_q[14:12], rd, register_1_q[6:0]}));  // open: en, clr
  imm_gen imm_gen_1 (
    .ImmSel(3'b000), .inst({register_1_q[31:20], rs1, register_1_q[14:12], rd, register_1_q[6:0]}), .imm(imm));
  regfile_main RegFile (
    .rd(rd), .Read_Data_1(RegFile_read_data_1), .ra(ra), .sp(sp), .t0(t0), .t1(t1), .t2(t2), .s0(s0),
    .s1(s1), .a0(a0), .rs1(rs1), .Write_Data(aluR), .RegWEn(1'b1), .clk(CLOCK));  // open: rs2, Read_Data_2
  alu Arithmetic_Logic_Unit (.Result(aluR), .ALUSel(4'b0000), .A(RegFile_read_data_1), .B(imm));
  // mem_main DMEM: pin names not known; wires that end beside it: DMEM_p1

  // Other names for the same wires on the sheet: clk = CLOCK

  // Notes on the sheet:
  //   Output
  //   IMEM (do **NOT** move this)
  //   Inputs
  //   It is OK to move the PC, RegFile, ALU, MEM, Branch Comp, Imm Gen, and Control Logic to wherever is most convenient for you when constructing your CPU, and to delete this text
  //   Inputs/Outputs for testing. Do **NOT** move these.
endmodule
