// Logisim project imm_gen.circ as structural Verilog: 1 circuit, main circuit imm_gen
module imm_gen (
  input  [31:0] inst,
  input  [2:0] ImmSel,
  output [31:0] imm
);

  wire [31:0] I, S, SB, U, UJ;

  assign I = {{20{inst[31]}}, inst[31:20]};  // Bit_Extender bit_extender_1
  assign S = {{20{inst[31]}}, {inst[31:25], inst[11:7]}};  // Bit_Extender bit_extender_2
  assign SB = {{19{inst[31]}}, {inst[31], inst[7], inst[30:25], inst[11:8], 1'b0}};  // Bit_Extender bit_extender_3
  Bit_Extender #(.in_width(32), .out_width(32), .\type ("input")) bit_extender_4 (
    .in({inst[31:12], {12{1'b0}}}), .out(U));  // open: extend
  assign UJ = {{11{inst[31]}}, {inst[31], inst[19:12], inst[20], inst[30:21], 1'b0}};  // Bit_Extender bit_extender_5
  Multiplexer #(.select(3), .width(32), .enable("false")) multiplexer_1 (
    .in0(I), .in1(S), .in2(SB), .in3(U), .in4(UJ), .out(imm), .sel(ImmSel));  // open: in5, in6, in7

  // Notes on the sheet:
  //   INPUTS to your circuit
  //   DON'T CHANGE THE LOCATIONS OF THE INPUTS AND OUTPUTS!
  //   OUTPUT from your circuit
endmodule
