// Logisim project regfile.circ as structural Verilog: 1 circuit, main circuit main
module main (
  input  [4:0] rs1,
  input  [4:0] rs2,
  input  [4:0] rd,
  input  [31:0] Write_Data,
  input  RegWEn,
  input  clk,
  output [31:0] ra,
  output [31:0] sp,
  output [31:0] t0,
  output [31:0] t1,
  output [31:0] t2,
  output [31:0] s0,
  output [31:0] s1,
  output [31:0] a0,
  output [31:0] Read_Data_1,
  output [31:0] Read_Data_2
);

  wire w1, w2, w5, w6, w7, w8, w9, w10;
  wire [31:0] x0, x1, x2, x5, x6, x7, x8, x9, x10;

  Demultiplexer #(.select(5), .enable("false")) demultiplexer_1 (
    .out1(w1), .out2(w2), .out5(w5), .out6(w6), .out7(w7), .out8(w8), .out9(w9), .out10(w10), .in(RegWEn),
    .sel(rd));  // open: out0, out3, out4, out11, out12, out13, out14, out15, out16, out17, out18, out19, out20, out21, out22, out23, out24, out25, out26, out27, out28, out29, out30, out31
  Demultiplexer #(.select(5), .width(32), .enable("false")) demultiplexer_2 (
    .out1(x1), .out2(x2), .out5(x5), .out6(x6), .out7(x7), .out8(x8), .out9(x9), .out10(x10),
    .in(Write_Data), .sel(rd));  // open: out0, out3, out4, out11, out12, out13, out14, out15, out16, out17, out18, out19, out20, out21, out22, out23, out24, out25, out26, out27, out28, out29, out30, out31
  Register #(.width(32)) register_1 (.D(x1), .en(w1), .clk(clk), .Q(ra));  // open: clr
  Register #(.width(32)) register_2 (.D(x2), .en(w2), .clk(clk), .Q(sp));  // open: clr
  Register #(.width(32)) register_3 (.D(x5), .en(w5), .clk(clk), .Q(t0));  // open: clr
  Register #(.width(32)) register_4 (.D(x6), .en(w6), .clk(clk), .Q(t1));  // open: clr
  Register #(.width(32)) register_5 (.D(x7), .en(w7), .clk(clk), .Q(t2));  // open: clr
  Register #(.width(32)) register_6 (.D(x8), .en(w8), .clk(clk), .Q(s0));  // open: clr
  Register #(.width(32)) register_7 (.D(x9), .en(w9), .clk(clk), .Q(s1));  // open: clr
  Register #(.width(32)) register_8 (.D(x10), .en(w10), .clk(clk), .Q(a0));  // open: clr
  Register #(.width(32)) register_9 (.D({32{1'b0}}), .clk(clk), .Q(x0));  // open: en, clr
  Multiplexer #(.select(5), .width(32), .enable("false")) multiplexer_1 (
    .in0(x0), .in1(ra), .in2(sp), .in5(t0), .in6(t1), .in7(t2), .in8(s0), .in9(s1), .in10(a0),
    .out(Read_Data_1), .sel(rs1));  // open: in3, in4, in11, in12, in13, in14, in15, in16, in17, in18, in19, in20, in21, in22, in23, in24, in25, in26, in27, in28, in29, in30, in31
  Multiplexer #(.select(5), .width(32), .enable("false")) multiplexer_2 (
    .in0(x0), .in1(ra), .in2(sp), .in5(t0), .in6(t1), .in7(t2), .in8(s0), .in9(s1), .in10(a0),
    .out(Read_Data_2), .sel(rs2));  // open: in3, in4, in11, in12, in13, in14, in15, in16, in17, in18, in19, in20, in21, in22, in23, in24, in25, in26, in27, in28, in29, in30, in31

  // Other names for the same wires on the sheet: read_data1[31:0] = Read_Data_1; read_data2[31:0] = Read_Data_2;
  //   read_reg1[4:0] = rs1; read_reg2[4:0] = rs2; write_en = RegWEn; write_reg[4:0] = rd

  // Notes on the sheet:
  //   INPUTS to your circuit
  //   DON'T CHANGE THE LOCATIONS OF THE INPUTS AND OUTPUTS!
  //   These are DEBUG/TEST outputs from your circuit.
  //   OUTPUTS from your circuit
endmodule
